// Logisim project Aluop.circ as structural Verilog
module Aluop (
  input  R,
  input  I,
  input  S,
  input  Lw,
  input  Auipc,
  input  Lui,
  input  Jal,
  input  Jalr,
  output [2:0] out_9
);

  wire not_1_out, not_2_out, not_3_out, not_4_out, not_5_out, not_6_out, not_7_out, not_8_out, not_9_out,
       not_10_out, not_11_out, not_12_out;

  not not_1 (not_1_out, R);
  not not_2 (not_2_out, I);
  not not_3 (not_3_out, Lw);
  not not_4 (not_4_out, Jalr);
  not not_5 (not_5_out, R);
  not not_6 (not_6_out, S);
  not not_7 (not_7_out, Lw);
  not not_8 (not_8_out, Auipc);
  not not_9 (not_9_out, R);
  not not_10 (not_10_out, I);
  not not_11 (not_11_out, S);
  not not_12 (not_12_out, Lui);
  and and_1 (out_9[2], not_1_out, not_2_out, not_3_out, not_4_out);
  and and_2 (out_9[1], not_5_out, not_6_out, not_7_out, not_8_out);
  and and_3 (out_9[0], not_9_out, not_10_out, not_11_out, not_12_out);
endmodule
