// Logisim project CPU.circ as structural Verilog: 1 circuit, main circuit main
module main (
  input  in_1,
  output [31:0] out_2,
  output [31:0] out_3,
  output [4:0] out_4,
  output [31:0] out_5
);

  wire clock_1_out, main_1_out_3, main_1_out_4, main_1_out_5, main_1_out_7, main_1_out_8, main_1_out_9,
       main_5_out_4;
  wire [1:0] main_1_out_6, main_1_out_10, main_1_out_12;
  wire [2:0] main_1_out_11;
  wire [3:0] alucontrol_1_out_4;
  wire [31:0] adder_1_out, main_2_b, main_2_j, main_2_out_4, main_3_out_8, multiplexer_1_out,
       multiplexer_2_out, multiplexer_3_out, multiplexer_4_out, ram_1_data, register_1_q, rom_1_data;

  Multiplexer #(.select(2), .width(32)) multiplexer_1 (
    .in0(adder_1_out), .in1(main_2_b), .in2(main_2_j), .in3(out_2), .out(multiplexer_1_out),
    .sel(main_1_out_10));  // open: en
  Clock clock_1 (.out(clock_1_out));
  Register #(.width(32)) register_1 (
    .D(multiplexer_1_out), .Q(register_1_q), .clk(clock_1_out), .clr(in_1));  // open: en
  Adder #(.width(32)) adder_1 (.a(register_1_q), .b(32'h4), .out(adder_1_out));  // open: cin, cout
  ROM #(.addrWidth(10), .dataWidth(32)) rom_1 (
    .addr(register_1_q[11:2]), .data({rom_1_data[31:25], out_4, rom_1_data[19:0]}));  // open: sel
  Control_main main_1 (
    .in_1(rom_1_data[6:0]), .out_5(main_1_out_5), .out_6(main_1_out_6), .out_7(main_1_out_7),
    .out_8(main_1_out_8), .out_9(main_1_out_9), .out_10(main_1_out_10), .out_12(main_1_out_12),
    .out_11(main_1_out_11), .out_3(main_1_out_3), .out_4(main_1_out_4), .in_2(main_5_out_4));
  Immediate_main main_2 (
    .in_1({rom_1_data[31:25], out_4, rom_1_data[19:0]}), .in_3(register_1_q), .out_4(main_2_out_4),
    .J(main_2_j), .in_2(main_1_out_6), .B(main_2_b));
  RegFile_main main_3 (
    .in_1(out_3), .out_8(main_3_out_8), .out_9(out_5), .in_3(rom_1_data[11:7]), .in_4(rom_1_data[19:15]),
    .in_5(out_4), .in_6(clock_1_out), .in_7(in_1), .in_2(main_1_out_4));
  AluControl alucontrol_1 (
    .in_1(main_1_out_11), .in_2(rom_1_data[14:12]), .FUNC7(rom_1_data[30]), .out_4(alucontrol_1_out_4));
  Multiplexer #(.select(2), .width(32)) multiplexer_2 (
    .in0(main_3_out_8), .in1(register_1_q), .in2(adder_1_out), .in3(main_3_out_8), .out(multiplexer_2_out),
    .sel(main_1_out_12));  // open: en
  Multiplexer #(.width(32)) multiplexer_3 (
    .in0(out_5), .in1(main_2_out_4), .out(multiplexer_3_out), .sel(main_1_out_5));  // open: en
  ALU_main main_4 (.in_1(multiplexer_2_out), .in_2(multiplexer_3_out), .in_3(alucontrol_1_out_4), .out_4(out_2));
  BranchAlu_main main_5 (.in_1(main_3_out_8), .in_2(out_5), .out_4(main_5_out_4), .in_3(rom_1_data[14:12]));
  RAM #(.addrWidth(10), .dataWidth(32), .bus("separate")) ram_1 (
    .addr(out_2[11:2]), .din(out_5), .data(ram_1_data), .str(main_1_out_9), .clk(clock_1_out),
    .ld(main_1_out_7), .clr(in_1));  // open: sel
  Multiplexer #(.width(32)) multiplexer_4 (
    .in0(out_2), .in1(ram_1_data), .out(multiplexer_4_out), .sel(main_1_out_8));  // open: en
  Multiplexer #(.width(32)) multiplexer_5 (
    .in0(multiplexer_4_out), .in1(adder_1_out), .out(out_3), .sel(main_1_out_3));  // open: en

  // Notes on the sheet:
  //   contents of rom_1 (hex, n*v repeats v):
  //   600693 d02223 d02423 402703 670713
endmodule
