// Logisim project Mux.circ as structural Verilog: 1 circuit, main circuit main
module main (
  input  a,
  input  Sel,
  input  b,
  output out_4
);

  wire and_1_out, and_2_out, not_1_out;

  not not_1 (not_1_out, Sel);
  and and_1 (and_1_out, a, not_1_out);
  and and_2 (and_2_out, Sel, b);
  or or_1 (out_4, and_1_out, and_2_out);
endmodule
