// Logisim project TypeDecode.circ as structural Verilog: 1 circuit, main circuit main
module main (
  input  [6:0] in_1,
  output R,
  output I,
  output S,
  output Lui,
  output B,
  output JALr,
  output LW,
  output Auipc,
  output Jal
);

  Comparator #(.width(7)) comparator_1 (.a(in_1), .b(7'b0110011), .eq(R));  // open: gt, lt
  Comparator #(.width(7)) comparator_2 (.a(in_1), .b(7'b0010011), .eq(I));  // open: gt, lt
  Comparator #(.width(7)) comparator_3 (.a(in_1), .b(7'b0100011), .eq(S));  // open: gt, lt
  Comparator #(.width(7)) comparator_4 (.a(in_1), .b(7'b0110111), .eq(Lui));  // open: gt, lt
  Comparator #(.width(7)) comparator_5 (.a(in_1), .b(7'b1100011), .eq(B));  // open: gt, lt
  Comparator #(.width(7)) comparator_6 (.a(in_1), .b(7'b1100111), .eq(JALr));  // open: gt, lt
  Comparator #(.width(7)) comparator_7 (.a(in_1), .b(7'b0000011), .eq(LW));  // open: gt, lt
  Comparator #(.width(7)) comparator_8 (.a(in_1), .b(7'b0010111), .eq(Auipc));  // open: gt, lt
  Comparator #(.width(7)) comparator_9 (.a(in_1), .b(7'b1101111), .eq(Jal));  // open: gt, lt
endmodule
